# Fritzing sketch distributeurChat (saved by Fritzing 0.9.2b)
circuit board: 4.06556cm x 4.32675cm
breadboards: 1

parts:
  D1 = Rectifier Diode [part_number=1N4001 package="300 mil [THT]"]
  TIP120 = Voltage Regulator - 5V [package="TO220 [THT]"]
  Moteur = DC Motor
  R1 = Resistor [tolerance=±5% resistance=2.2k package=THT]
  Arduino_Pro_mini = Arduino Pro Mini v13
  J2 = male pin header, 6 pins [form="♂ (male)"]
  R2 = Resistor [tolerance=±5% resistance=2k package=THT]
  Rotary = female pin header, 3 pins [form="♀ (female)"]
  - = female pin header, 1 pin [form="♀ (female)"]
  + = female pin header, 1 pin [form="♀ (female)"]
  J3 = male pin header, 6 pins [form="♂ (male)"]
  GND = female pin header, 2 pins [form="♀ (female)"]

nets:
  N1: D1.cathode, Moteur.pin_1, Arduino_Pro_mini.RAW, +.pin1
  N2: D1.anode, TIP120.GND, Moteur.pin_2
  N3: TIP120.input_voltage, R1.Pin_0
  N4: TIP120.output_voltage, Arduino_Pro_mini.GND, J2.pin6, R2.Pin_1, -.pin1, J3.pin1, GND.pin1, GND.pin2
  N5: R1.Pin_1, Arduino_Pro_mini.D3_PWM
  N6: Arduino_Pro_mini.VCC, J3.pin2
  N7: Arduino_Pro_mini.A2, Rotary.pin1
  N8: Arduino_Pro_mini.A1, Rotary.pin2
  N9: Arduino_Pro_mini.A0, Rotary.pin3
  N10: Arduino_Pro_mini.D12/MISO, J3.pin4
  N11: Arduino_Pro_mini.D11_PWM/MOSI, J3.pin5
  N12: Arduino_Pro_mini.D10_PWM/SS, J3.pin6
  N13: Arduino_Pro_mini.D9_PWM, J2.pin5
  N14: Arduino_Pro_mini.D7, J2.pin4
  N15: Arduino_Pro_mini.D6_PWM, J2.pin3
  N16: Arduino_Pro_mini.D5_PWM, J2.pin2
  N17: Arduino_Pro_mini.D4, J2.pin1
  N18: R2.Pin_0, J3.pin3

notes:
  LCD2
  LCD1
  croquette v1.0
